# Fritzing sketch SNES (saved by Fritzing 0.9.3b)
breadboards: 1

parts:
  Part1 = Adafruit Trinket M0 [part_number="Adafruit #3500"]
  Part2 = TXB0104 4-channel Bi-Directional Level Shifter
  J1 = shrouded pin header, 10 pins [form="♂ (shrouded male)"]
  S1 = Pushbutton [package="[THT]"]

nets:
  GND: Part1.GND, Part2.GND, J1.pin1, S1.Pin_1, S1.Pin_2
  N1: Part1.D4_A2_PA06_TXD_MOSI, Part2.A3
  N2: Part1.D3_A3_PA07_RXD_SCK, Part2.A2
  N3: Part1.3.3V, Part2.LV
  N4: Part1.D2_A1_PA09_SCL_MISO, S1.Pin_3, S1.Pin_4
  N5: Part1.D0_A4_PA08_SDA, Part2.A1
  N6: Part2.HV, J1.pin2
  N7: Part2.B1, J1.pin3
  N8: Part2.B2, J1.pin4
  N9: Part2.B3, J1.pin5

custom parts:
  TXB0104 4-channel Bi-Directional Level Shifter: Because the Arduino (and Basic Stamp) are 5V devices, and most modern sensors, displays, flash cards and modes are 3.3V-only, many makers find that they need to perform level shifting/conversion to protect the 3.3V device from 5V. Although one can use resistors to make a divider, for high speed transfers, the resistors can add a lot of slew and cause havoc that is tough to debug. For that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
